// Digital circuit BS_ALU.dig as structural Verilog
module BS_ALU (
  input  A,
  input  B,
  input  C,
  input  I0,
  input  I1,
  output Fout,
  output Cout
);

  wire nand_1_out, nand_2_out, nand_4_out, nand_5_out, xor_1_out, xor_2_out;

  xor xor_1 (xor_1_out, A, B);
  nand nand_1 (nand_1_out, A, B);
  xor xor_2 (xor_2_out, xor_1_out, C);
  nand nand_2 (nand_2_out, xor_1_out, C);
  nand nand_3 (Cout, nand_2_out, nand_1_out);
  nand nand_4 (nand_4_out, xor_2_out, I0);
  nand nand_5 (nand_5_out, I1, Cout);
  nand nand_6 (Fout, nand_4_out, nand_5_out);

  // Notes on the sheet:
  //   BIT SERIAL ALU
  //   FULL ADDER
  //   MULTIPLEXER
endmodule
