// Digital circuit shrek_logic_4.dig as structural Verilog
module shrek_logic_4 (
  input  CY,
  input  T1,
  input  nT0,
  input  IR6,
  input  SUM,
  input  nY0,
  input  nY1,
  input  nY2,
  input  nY3,
  input  nY5,
  input  nY7,
  input  CS,
  output Cout,
  output CLR,
  output nB,
  output I0,
  output I1,
  output CSET,
  output CRES,
  output Fout
);

  wire nand_1_out, nand_2_out, nand_3_out, nand_6_out, nand_10_out, nand_11_out, nand_12_out;

  nand nand_1 (nand_1_out, nY1, nY2, nY3);
  nand nand_2 (nand_2_out, CY, IR6);
  nand nand_3 (nand_3_out, nand_1_out, nand_2_out);
  nand nand_4 (I1, nY1, nY2);
  nand nand_5 (nB, nY5, nY5);
  nand nand_6 (nand_6_out, nY0, nY7);
  nand nand_7 (CSET, T1, nY5);
  nand nand_8 (CRES, nT0, nY5);
  nand nand_9 (CLR, nand_6_out, nT0);
  nand nand_10 (nand_10_out, CS, nand_3_out);
  nand nand_11 (nand_11_out, nand_3_out, nY1);
  nand nand_12 (nand_12_out, I1, SUM);
  nand nand_13 (Cout, nand_10_out, nand_10_out);
  nand nand_14 (Fout, nand_11_out, nand_12_out);

  assign I0 = nY1;

  // Notes on the sheet:
  //   INSTRUCTION DECODER
  //   DETECT AND,OR,XOR
  //   SUBTRACT
  //   Carry Suppress
  //   OUTPUT MULTIPLEXER
endmodule
